# Fritzing sketch LightGame (saved by Fritzing 0.9.3b)
breadboards: 1

parts:
  Part1 = Arduino Uno (Rev3)
  LED1 = smd LED [color="Green (555nm)" package="1206 [SMD]"]
  LED2 = smd LED [color="Green (555nm)" package="1206 [SMD]"]
  LED3 = smd LED [color="Yellow (585nm)" package="1206 [SMD]"]
  LED4 = smd LED [color="Yellow (585nm)" package="1206 [SMD]"]
  LED5 = smd LED [color="Red (635nm)" package="1206 [SMD]"]
  LED6 = smd LED [color="Yellow (585nm)" package="1206 [SMD]"]
  LED7 = smd LED [color="Yellow (585nm)" package="1206 [SMD]"]
  LED8 = smd LED [color="Green (555nm)" package="1206 [SMD]"]
  LED9 = smd LED [color="Green (555nm)" package="1206 [SMD]"]
  S1 = Pushbutton [package="[THT]"]
  R1 = Resistor [tolerance=±5% resistance=10k package="2512 [SMD]"]

nets:
  N1: Part1.D8, LED7.cathode
  N2: Part1.D9_PWM, LED8.cathode
  N3: Part1.D10_PWM/SS, LED9.cathode
  N4: Part1.D11_PWM/MOSI, S1.Pin_3, S1.Pin_4, R1.Pin_0
  N5: Part1.GND, R1.Pin_1
  N6: Part1.D2, LED1.cathode
  N7: Part1.D3_PWM, LED2.cathode
  N8: Part1.D4, LED3.cathode
  N9: Part1.D5_PWM, LED4.cathode
  N10: Part1.D6_PWM, LED5.cathode
  N11: Part1.D7, LED6.cathode
  N12: LED1.anode, LED2.anode, LED3.anode, LED4.anode, LED5.anode, LED6.anode, LED7.anode, LED8.anode, LED9.anode
  N13: S1.Pin_1, S1.Pin_2

// code stored in the sketch: LightGame.ino
// Sample configuration for LEDs
/*int greenL1 = 2;
int greenL2 = 3;
int yellowL1 = 4;
int yellowL2 = 5;
int red = 6;
int yellowR2 = 7;
int yellowR1 = 8;
int greenR2 = 9;
int greenR1 = 10;*/
int button = 0; // Initialize button state
int light = 0;  // Initialize LED pin
void setup() {
  // put your setup code here, to run once:
  
  /* Lights are on pins 2-10, and button is on pin 11 */
  
  for(int i=2;i<11;i++){
    pinMode(i,OUTPUT);
  }
  pinMode(11,INPUT);
  
 // Start serial communication with baud rate 115,200 
 Serial.begin(115200);
 Serial.println("Begin!");
}

void loop() {
  // put your main code here, to run repeatedly:
  /* Cycle LEDs */
  for(int i=2; i<11; i++){
    light = i;  // Set LED pin to i
    button = digitalRead(11); // Read button state
    digitalWrite(light,HIGH); // Turn on LED at pin "light"
    
    /* Sample button 75 times */
    for(int j=0;j<75;j++){
      Serial.println(button); // Print button state (0 or 1) to serial monitor

      /* Flash current LED 4 times if the button is pressed */
      if(button==1){
        for(int k=0; k<4; k++){
          digitalWrite(light,LOW);
          delay(200);
          digitalWrite(light,HIGH);
          delay(200);
        }
        while(button==1){
          button = digitalRead(11); // Wait until button state is 0 before continuing
        }
        digitalWrite(light,LOW);  // Turn off LED
        delay(3000);  // Wait 3 seconds
      }
      delay(1); // Wait 1 ms
    }
    
    
    digitalWrite(light,LOW);  // Turn off LED and move to the next LED
  }
  

}
